# Fritzing sketch Schaltskizze (saved by Fritzing 0.9.3b)
breadboards: 1

parts:
  LEDRot = LED - 5mm [color="Red (660nm)" package="5 mm [THT]"]
  LEDGelb = LED - 5mm [color="Yellow (595nm)" package="5 mm [THT]"]
  LEDGrün = LED - 5mm [color="Green (570nm)" package="5 mm [THT]"]
  R1 = Resistor [tolerance=±5% resistance=220 package=THT]
  R2 = Resistor [tolerance=±5% resistance=220 package=THT]
  R3 = Resistor [tolerance=±5% resistance=220 package=THT]
  Raspberry_Pi_2 = Raspberry Pi 2

nets:
  N1: LEDRot.cathode, Raspberry_Pi_2.GPIO16
  N2: LEDRot.anode, R1.Pin_0
  N3: LEDGelb.cathode, Raspberry_Pi_2.GPIO20
  N4: LEDGelb.anode, R2.Pin_0
  N5: LEDGrün.cathode, Raspberry_Pi_2.GPIO21
  N6: LEDGrün.anode, R3.Pin_0
  N7: R1.Pin_1, R2.Pin_1, R3.Pin_1, Raspberry_Pi_2.GND
